# Fritzing sketch Nucleo F446 EG (saved by Fritzing 0.9.3b)
perfboards: 2
breadboards: 1

parts:
  J1 = STM32 Nucleo boards
  R1 = Rotary Potentiometer (Small) [maximum_resistance=100kΩ package=THT]  # not connected
  R2 = Rotary Potentiometer (Small) [maximum_resistance=100kΩ package=THT]  # not connected
  R3 = Rotary Potentiometer (Small) [maximum_resistance=100kΩ package=THT]  # not connected
  R4 = Rotary Potentiometer (Small) [maximum_resistance=100kΩ package=THT]  # not connected
  R5 = Rotary Potentiometer (Small) [maximum_resistance=100kΩ package=THT]  # not connected
  R6 = Rotary Potentiometer (Small) [maximum_resistance=100kΩ package=THT]  # not connected
  R7 = Rotary Potentiometer (Small) [maximum_resistance=100kΩ package=THT]  # not connected
  R8 = Rotary Potentiometer (Small) [maximum_resistance=100kΩ package=THT]  # not connected
  R9 = Resistor [tolerance=±5% resistance=1k package=THT]
  C1 = Film/Foil Capacitor [capacitance=100nF voltage=35V package="5mm [THT, pp]"]

nets:
  N1: J1.A2, R9.Pin_0
  N2: J1.GND#1189, C1.+
  N3: R9.Pin_1, C1.-

notes:
  Pulse Generator
  POT x 8 Panel
  CR LPF
  ADSR OUT
